// Logisim project trabalho_isa.circ as structural Verilog: 32 circuits, main circuit main
module main (
  output [11:0] out_1,
  output [11:0] out_2,
  output [11:0] out_3,
  output [11:0] out_4,
  output [11:0] out_5,
  output [11:0] out_6,
  output [11:0] out_7,
  output [11:0] out_8
);

  wire clock_1_out;

  Clock clock_1 (.out(clock_1_out));
  ISA isa_1 (
    .clk(clock_1_out), .r7(out_1), .r6(out_2), .r5(out_3), .r4(out_4), .r3(out_5), .r2(out_6), .r1(out_7),
    .r0(out_8));  // open: reset

  // Notes on the sheet:
  //   SUBCIRCUITO ISA 
endmodule

module ISA (
  input  reset,
  input  clk,
  output [11:0] r7,
  output [11:0] r6,
  output [11:0] r5,
  output [11:0] r4,
  output [11:0] r3,
  output [11:0] r2,
  output [11:0] r1,
  output [11:0] r0
);

  wire BGE_BLT_UC, clk_t, JAL_UC, Lt_Zero_ULA, OM_UC, RS2_UC, W_UC, WM_UC, Zero_ULA;
  wire [1:0] DATA_UC, IMM_UC, PC_UC, RD_UC, RS1_UC;
  wire [2:0] B_RS1, B_RS2, multiplexer_8_out, multiplexer_9_out, multiplexer_10_out, R_RS2;
  wire [3:0] OPCODE;
  wire [7:6] Instruction;
  wire [11:0] adder_1_out, adder_2_out, adder_3_out, b_reg_1_b, IMM_B, IMM_I, IMM_J, multiplexer_1_out,
       multiplexer_2_out, multiplexer_3_out, multiplexer_4_out, multiplexer_5_out, multiplexer_6_out,
       multiplexer_7_out, multiplexer_11_out, multiplexer_12_out, PC, PC_p1, RA, ram_1_dout, ula_1_r;

  Adder #(.width(12)) adder_1 (.a(PC), .b(IMM_B), .out(adder_1_out));  // open: cin, cout
  Adder #(.width(12)) adder_2 (.a(IMM_I), .b(RA), .out(adder_2_out));  // open: cin, cout
  Adder #(.width(12)) adder_3 (.a(IMM_J), .b(PC), .out(adder_3_out));  // open: cin, cout
  Multiplexer #(.width(12)) multiplexer_1 (.in0(adder_2_out), .in1(adder_3_out), .out(multiplexer_1_out), .sel(JAL_UC));
  Multiplexer #(.width(12)) multiplexer_2 (.in0(PC_p1), .in1(adder_1_out), .out(multiplexer_2_out), .sel(Lt_Zero_ULA));
  Multiplexer #(.width(12)) multiplexer_3 (.in0(adder_1_out), .in1(PC_p1), .out(multiplexer_3_out), .sel(Lt_Zero_ULA));
  Multiplexer #(.width(12)) multiplexer_4 (.in0(PC_p1), .in1(adder_1_out), .out(multiplexer_4_out), .sel(Zero_ULA));
  Multiplexer #(.width(12)) multiplexer_5 (
    .in0(multiplexer_2_out), .in1(multiplexer_3_out), .out(multiplexer_5_out), .sel(BGE_BLT_UC));
  Multiplexer #(.select(2), .width(12)) multiplexer_6 (
    .in0(multiplexer_5_out), .in1(multiplexer_1_out), .in2(multiplexer_4_out), .in3(PC_p1),
    .out(multiplexer_6_out), .sel(PC_UC));
  Multiplexer #(.width(12)) multiplexer_7 (
    .in0(multiplexer_6_out), .in1({12{1'b0}}), .out(multiplexer_7_out), .sel(reset));
  add12b add12b_1 (.A(12'h1), .B(PC), .R(PC_p1));  // open: OVF
  PC pc_1 (.IP(multiplexer_7_out), .clk(clk_t), .P_ROM(PC));
  ROM #(.addrWidth(12), .dataWidth(12)) rom_1 (.addr(PC), .data({Instruction, B_RS2, B_RS1, OPCODE}));
  UC uc_1 (
    .OPCODE(OPCODE), .W(W_UC), .RS1(RS1_UC), .WM(WM_UC), .RS2(RS2_UC), .IMM(IMM_UC), .DATA(DATA_UC),
    .OM(OM_UC), .JAL(JAL_UC), .PC(PC_UC), .RD(RD_UC), .BGE_BLT(BGE_BLT_UC));
  // Probe on OPCODE
  assign IMM_J = {{7{Instruction[7]}}, {Instruction, B_RS2}};  // Bit_Extender bit_extender_1
  // Probe on {Instruction, B_RS2}
  Clock clock_1 (.out(clk_t));
  unsig_ext unsig_ext_1 (.A(Instruction), .R(R_RS2));
  unsig_ext_2b unsig_ext_2b_1 (.A(Instruction), .R(IMM_B));
  unsig_ext_2b unsig_ext_2b_2 (.A(Instruction), .R(IMM_I));
  Multiplexer #(.select(2), .width(3)) multiplexer_8 (
    .in0(B_RS1), .in1(B_RS2), .in2(B_RS1), .in3(B_RS2), .out(multiplexer_8_out), .sel(RS1_UC));
  Multiplexer #(.width(3)) multiplexer_9 (.in0(R_RS2), .in1(B_RS2), .out(multiplexer_9_out), .sel(RS2_UC));
  Multiplexer #(.select(2), .width(3)) multiplexer_10 (
    .in0(B_RS1), .in1(B_RS1), .in2(B_RS1), .out(multiplexer_10_out), .sel(RD_UC));  // open: in3
  B_REG b_reg_1 (
    .rd(multiplexer_10_out), .rs1(multiplexer_8_out), .rs2(multiplexer_9_out), .D(multiplexer_12_out),
    .W(W_UC), .clk(clk_t), .a(RA), .b(b_reg_1_b), .vr0(r0), .vr1(r1), .vr2(r2), .vr3(r3), .vr4(r4), .vr5(r5),
    .vr6(r6), .vr7(r7));
  // Probe on r7
  // Probe on r6
  // Probe on r5
  // Probe on r4
  // Probe on r3
  // Probe on r2
  // Probe on r1
  // Probe on r0
  Multiplexer #(.select(2), .width(12)) multiplexer_11 (
    .in0(b_reg_1_b), .in1(IMM_I), .in2(IMM_J), .in3(IMM_B), .out(multiplexer_11_out), .sel(IMM_UC));
  ULA ula_1 (.A(RA), .B(multiplexer_11_out), .S(OPCODE), .is_ZERO(Zero_ULA), .R(ula_1_r), .is_lt_ZERO(Lt_Zero_ULA));
  Multiplexer #(.select(2), .width(12)) multiplexer_12 (
    .in0(ula_1_r), .in1(ram_1_dout), .in2(PC_p1), .out(multiplexer_12_out), .sel(DATA_UC));  // open: in3
  RAM #(.addrWidth(12), .dataWidth(12)) ram_1 (
    .addr(ula_1_r), .we(WM_UC), .oe(OM_UC), .clk(clk_t), .din(b_reg_1_b), .dout(ram_1_dout));

  // Other names for the same wires on the sheet: I_RD[2:0] = B_RS1; Instruction[5:0] = {B_RS2, B_RS1};
  //   J_RS1[2:0] = B_RS1; R_RD[2:0] = B_RS1; I_RS1[2:0] = B_RS2; R_RS1[2:0] = B_RS2

  // Notes on the sheet:
  //   BLT
  //   BGE
  //   2. BEQ
  //   3. PC +1
  //   0. BGE ou BLT
  //   1.  JAL ou JALR
  //   contents of rom_1 (hex, n*v repeats v):
  //   2c 4c 3c4 124 a7d 626 0 0 620
  //   formato R
  //   formato B
  //   formato I
  //   formato J
endmodule

module B_REG (
  input  [2:0] rd,
  input  [2:0] rs1,
  input  [2:0] rs2,
  input  [11:0] D,
  input  W,
  input  clk,
  output [11:0] a,
  output [11:0] b,
  output [11:0] vr0,
  output [11:0] vr1,
  output [11:0] vr2,
  output [11:0] vr3,
  output [11:0] vr4,
  output [11:0] vr5,
  output [11:0] vr6,
  output [11:0] vr7
);

  wire w1, w2, w3, w4, w5, w6, w7;
  wire [11:0] multiplexer_1_out, multiplexer_2_out, multiplexer_3_out, multiplexer_4_out, multiplexer_5_out,
       multiplexer_6_out, multiplexer_7_out;

  Demultiplexer #(.select(3)) demultiplexer_1 (
    .out1(w1), .out2(w2), .out3(w3), .out4(w4), .out5(w5), .out6(w6), .out7(w7), .in(W), .sel(rd));  // open: out0
  Multiplexer #(.width(12)) multiplexer_1 (.in0(vr1), .in1(D), .out(multiplexer_1_out), .sel(w1));
  Multiplexer #(.width(12)) multiplexer_2 (.in0(vr2), .in1(D), .out(multiplexer_2_out), .sel(w2));
  Multiplexer #(.width(12)) multiplexer_3 (.in0(vr3), .in1(D), .out(multiplexer_3_out), .sel(w3));
  Multiplexer #(.width(12)) multiplexer_4 (.in0(vr4), .in1(D), .out(multiplexer_4_out), .sel(w4));
  Multiplexer #(.width(12)) multiplexer_5 (.in0(vr5), .in1(D), .out(multiplexer_5_out), .sel(w5));
  Multiplexer #(.width(12)) multiplexer_6 (.in0(vr6), .in1(D), .out(multiplexer_6_out), .sel(w6));
  Multiplexer #(.width(12)) multiplexer_7 (.in0(vr7), .in1(D), .out(multiplexer_7_out), .sel(w7));
  Register #(.width(12)) R1 (.D(multiplexer_1_out), .clk(clk), .Q(vr1));  // open: en, clr
  Register #(.width(12)) R2 (.D(multiplexer_2_out), .clk(clk), .Q(vr2));  // open: en, clr
  Register #(.width(12)) R3 (.D(multiplexer_3_out), .clk(clk), .Q(vr3));  // open: en, clr
  Register #(.width(12)) R4 (.D(multiplexer_4_out), .clk(clk), .Q(vr4));  // open: en, clr
  Register #(.width(12)) R5 (.D(multiplexer_5_out), .clk(clk), .Q(vr5));  // open: en, clr
  Register #(.width(12)) R6 (.D(multiplexer_6_out), .clk(clk), .Q(vr6));  // open: en, clr
  Register #(.width(12)) R7 (.D(multiplexer_7_out), .clk(clk), .Q(vr7));  // open: en, clr
  Multiplexer #(.select(3), .width(12)) multiplexer_8 (
    .in0({12{1'b0}}), .in1(vr1), .in2(vr2), .in3(vr3), .in4(vr4), .in5(vr5), .in6(vr6), .in7(vr7), .out(a),
    .sel(rs1));
  Multiplexer #(.select(3), .width(12)) multiplexer_9 (
    .in0({12{1'b0}}), .in1(vr1), .in2(vr2), .in3(vr3), .in4(vr4), .in5(vr5), .in6(vr6), .in7(vr7), .out(b),
    .sel(rs2));

  assign vr0 = {12{1'b0}};

  // Notes on the sheet:
  //   R0
endmodule

module ULA (
  input  [11:0] A,
  input  [11:0] B,
  input  [3:0] S,
  output is_ZERO,
  output [11:0] R,
  output is_lt_ZERO
);

  wire [11:0] add12b_1_r, and12b_1_r, not12b_1_r, or12b_1_r, sll12b_1_r, srl12b_1_r, sub12b_1_r0, xor12b_1_r;

  not12b not12b_1 (.A(A), .R(not12b_1_r));
  and12b and12b_1 (.A(A), .B(B), .R(and12b_1_r));
  or12b or12b_1 (.A(A), .B(B), .R(or12b_1_r));
  xor12b xor12b_1 (.A(A), .B(B), .R(xor12b_1_r));
  add12b add12b_1 (.A(A), .B(B), .R(add12b_1_r));  // open: OVF
  sub12b sub12b_1 (.A(A), .B(B), .R0(sub12b_1_r0));  // open: OVF
  SLL12b sll12b_1 (.A(A), .B(B), .R(sll12b_1_r));
  SRL12b srl12b_1 (.A(A), .B(B), .R(srl12b_1_r));
  Multiplexer #(.select(4), .width(12)) multiplexer_1 (
    .in0(sub12b_1_r0), .in4(add12b_1_r), .in6(sub12b_1_r0), .in7(sub12b_1_r0), .in8(not12b_1_r),
    .in9(and12b_1_r), .in10(or12b_1_r), .in11(xor12b_1_r), .in12(add12b_1_r), .in13(sub12b_1_r0),
    .in14(sll12b_1_r), .in15(srl12b_1_r), .out(R), .sel(S));  // open: in1, in2, in3, in5
  or_aux_ula or_aux_ula_1 (.A(R), .tell_if_ZERO(is_ZERO));
  is_lt_0 is_lt_0_1 (.A(R), .R(is_lt_ZERO));

  // Notes on the sheet:
  //   ARRUMAR_SHIFT_!!
endmodule

module PC (
  input  [11:0] IP,
  input  clk,
  output [11:0] P_ROM
);

  Register #(.width(12)) register_1 (.D(IP), .clk(clk), .Q(P_ROM));  // open: en, clr
endmodule

module UC (
  input  [3:0] OPCODE,
  output W,
  output [1:0] RS1,
  output WM,
  output RS2,
  output [1:0] IMM,
  output [1:0] DATA,
  output OM,
  output JAL,
  output [1:0] PC,
  output [1:0] RD,
  output BGE_BLT
);

  W_UC w_uc_1 (.A(OPCODE[3]), .B(OPCODE[2]), .C(OPCODE[1]), .D(OPCODE[0]), .W(W));
  WM_UC wm_uc_1 (.A(OPCODE[3]), .B(OPCODE[2]), .C(OPCODE[1]), .D(OPCODE[0]), .W(WM));
  IMM_UC imm_uc_1 (.A(OPCODE[3]), .B(OPCODE[2]), .C(OPCODE[1]), .D(OPCODE[0]), .IMM_0(IMM[0]), .IMM_1(IMM[1]));
  OM_UC om_uc_1 (.A(OPCODE[3]), .B(OPCODE[2]), .C(OPCODE[1]), .D(OPCODE[0]), .OW(OM));
  PC_UC pc_uc_1 (.A(OPCODE[3]), .B(OPCODE[2]), .C(OPCODE[1]), .D(OPCODE[0]), .PC_0(PC[0]), .PC_1(PC[1]));
  BGE_BLT_UC bge_blt_uc_1 (.A(OPCODE[3]), .B(OPCODE[2]), .C(OPCODE[1]), .D(OPCODE[0]), .R(BGE_BLT));
  RS1_UC rs1_uc_1 (.A(OPCODE[3]), .B(OPCODE[2]), .C(OPCODE[1]), .D(OPCODE[0]), .RS1_0(RS1[0]), .RS1_1(RS1[1]));
  RS2_UC rs2_uc_1 (.A(OPCODE[3]), .B(OPCODE[2]), .C(OPCODE[1]), .D(OPCODE[0]), .RS2(RS2));
  DATA_UC data_uc_1 (.A(OPCODE[3]), .B(OPCODE[2]), .C(OPCODE[1]), .D(OPCODE[0]), .DATA_0(DATA[0]), .DATA_1(DATA[1]));
  JAL_UC jal_uc_1 (.A(OPCODE[3]), .B(OPCODE[2]), .C(OPCODE[1]), .D(OPCODE[0]), .JAL(JAL));
  RD_UC rd_uc_1 (.A(OPCODE[3]), .B(OPCODE[2]), .C(OPCODE[1]), .D(OPCODE[0]), .RD_0(RD[0]), .RD_1(RD[1]));

  // Other names for the same wires on the sheet: OP_0 = OPCODE[0]; OP_1 = OPCODE[1]; OP_2 = OPCODE[2];
  //   OP_3 = OPCODE[3]
endmodule

module WM_UC (
  input  A,
  input  B,
  input  C,
  input  D,
  output W
);

  wire not_1_out, not_2_out;

  not not_1 (not_1_out, A);
  not not_2 (not_2_out, B);
  and and_1 (W, not_1_out, not_2_out, C, D);
endmodule

module W_UC (
  input  A,
  input  B,
  input  C,
  input  D,
  output W
);

  wire and_1_out, and_2_out, and_3_out, and_4_out, not_1_out, not_2_out, not_3_out, not_4_out, not_5_out,
       not_6_out, not_7_out, not_8_out, not_9_out, not_10_out, not_11_out;

  not not_1 (not_1_out, A);
  not not_2 (not_2_out, B);
  not not_3 (not_3_out, C);
  not not_4 (not_4_out, A);
  not not_5 (not_5_out, B);
  not not_6 (not_6_out, D);
  not not_7 (not_7_out, A);
  not not_8 (not_8_out, C);
  not not_9 (not_9_out, D);
  not not_10 (not_10_out, A);
  not not_11 (not_11_out, C);
  and and_1 (and_1_out, not_1_out, not_2_out, not_3_out, D);
  and and_2 (and_2_out, not_4_out, not_5_out, C, not_6_out);
  and and_3 (and_3_out, not_7_out, B, not_8_out, not_9_out);
  and and_4 (and_4_out, not_10_out, B, not_11_out, D);
  or or_1 (W, A, and_1_out, and_2_out, and_3_out, and_4_out);
endmodule

module IMM_UC (
  input  A,
  input  B,
  input  C,
  input  D,
  output IMM_0,
  output IMM_1
);

  wire and_1_out, and_2_out, and_3_out, and_4_out, and_5_out, and_6_out, and_7_out, and_8_out, not_1_out,
       not_2_out, not_3_out, not_4_out, not_5_out, not_6_out, not_7_out, not_8_out, not_9_out, not_10_out,
       not_11_out, not_12_out, not_13_out, not_14_out;

  not not_1 (not_1_out, A);
  not not_2 (not_2_out, C);
  not not_3 (not_3_out, A);
  not not_4 (not_4_out, D);
  not not_5 (not_5_out, A);
  not not_6 (not_6_out, B);
  not not_7 (not_7_out, D);
  not not_8 (not_8_out, A);
  not not_9 (not_9_out, A);
  not not_10 (not_10_out, B);
  not not_11 (not_11_out, C);
  not not_12 (not_12_out, A);
  not not_13 (not_13_out, A);
  not not_14 (not_14_out, D);
  and and_1 (and_1_out, not_1_out, B, not_2_out, D);
  and and_2 (and_2_out, not_3_out, B, C, not_4_out);
  and and_3 (and_3_out, not_5_out, not_6_out, not_7_out);
  and and_4 (and_4_out, not_8_out, C, D);
  and and_5 (and_5_out, A, B, C);
  and and_6 (and_6_out, not_9_out, not_10_out, not_11_out);
  and and_7 (and_7_out, not_12_out, C, D);
  and and_8 (and_8_out, not_13_out, B, not_14_out);
  or or_1 (IMM_1, and_6_out, and_7_out, and_8_out);
  or or_2 (IMM_0, and_1_out, and_2_out, and_3_out, and_4_out, and_5_out);
endmodule

module OM_UC (
  input  A,
  input  B,
  input  C,
  input  D,
  output OW
);

  wire not_1_out, not_2_out, not_3_out;

  not not_1 (not_1_out, A);
  not not_2 (not_2_out, B);
  not not_3 (not_3_out, D);
  and and_1 (OW, not_1_out, not_2_out, C, not_3_out);
endmodule

module PC_UC (
  input  A,
  input  B,
  input  C,
  input  D,
  output PC_0,
  output PC_1
);

  wire and_1_out, and_2_out, and_3_out, and_4_out, and_5_out, and_6_out, not_1_out, not_2_out, not_3_out,
       not_4_out, not_5_out, not_6_out, not_7_out, not_8_out, not_9_out, not_10_out, not_11_out, not_12_out,
       not_13_out;

  not not_1 (not_1_out, A);
  not not_2 (not_2_out, B);
  not not_3 (not_3_out, C);
  not not_4 (not_4_out, A);
  not not_5 (not_5_out, B);
  not not_6 (not_6_out, A);
  not not_7 (not_7_out, C);
  not not_8 (not_8_out, A);
  not not_9 (not_9_out, B);
  not not_10 (not_10_out, A);
  not not_11 (not_11_out, C);
  not not_12 (not_12_out, D);
  not not_13 (not_13_out, A);
  and and_1 (and_1_out, not_1_out, not_2_out, not_3_out, D);
  and and_2 (and_2_out, not_4_out, not_5_out, C);
  and and_3 (and_3_out, not_6_out, B, not_7_out);
  and and_4 (and_4_out, not_8_out, not_9_out, C);
  and and_5 (and_5_out, not_10_out, B, not_11_out, not_12_out);
  and and_6 (and_6_out, not_13_out, B, C, D);
  or or_1 (PC_0, and_1_out, and_2_out, and_3_out, A);
  or or_2 (PC_1, and_4_out, and_5_out, and_6_out, A);
endmodule

module RD_UC (
  input  A,
  input  B,
  input  C,
  input  D,
  output RD_0,
  output RD_1
);

  wire and_1_out, and_2_out, not_1_out, not_2_out, not_3_out, not_4_out, not_5_out;

  not not_1 (not_1_out, A);
  not not_2 (not_2_out, B);
  not not_3 (not_3_out, D);
  not not_4 (not_4_out, A);
  not not_5 (not_5_out, C);
  and and_1 (and_1_out, not_1_out, not_2_out, C, not_3_out);
  and and_2 (and_2_out, not_4_out, B, not_5_out, D);
  or or_1 (RD_1, and_1_out, and_2_out);

  assign RD_0 = A;
endmodule

module RS1_UC (
  input  A,
  input  B,
  input  C,
  input  D,
  output RS1_0,
  output RS1_1
);

  wire and_1_out, and_2_out, and_3_out, and_4_out, and_5_out, and_6_out, not_1_out, not_2_out, not_3_out,
       not_4_out, not_5_out, not_6_out, not_7_out, not_8_out, not_9_out, not_10_out, not_11_out, not_12_out,
       not_13_out;

  not not_1 (not_1_out, A);
  not not_2 (not_2_out, B);
  not not_3 (not_3_out, D);
  not not_4 (not_4_out, A);
  not not_5 (not_5_out, C);
  not not_6 (not_6_out, A);
  not not_7 (not_7_out, B);
  not not_8 (not_8_out, D);
  not not_9 (not_9_out, A);
  not not_10 (not_10_out, A);
  not not_11 (not_11_out, B);
  not not_12 (not_12_out, A);
  not not_13 (not_13_out, C);
  and and_1 (and_1_out, not_1_out, not_2_out, C, not_3_out);
  and and_2 (and_2_out, not_4_out, B, not_5_out, D);
  and and_3 (and_3_out, not_6_out, not_7_out, not_8_out);
  and and_4 (and_4_out, not_9_out, B, D);
  and and_5 (and_5_out, not_10_out, not_11_out, C, D);
  and and_6 (and_6_out, not_12_out, B, not_13_out, D);
  or or_1 (RS1_0, and_1_out, and_2_out, A);
  or or_2 (RS1_1, and_3_out, and_4_out, and_5_out, and_6_out);
endmodule

module RS2_UC (
  input  A,
  input  B,
  input  C,
  input  D,
  output RS2
);

  not not_1 (RS2, A);
endmodule

module DATA_UC (
  input  A,
  input  B,
  input  C,
  input  D,
  output DATA_0,
  output DATA_1
);

  wire not_1_out, not_2_out, not_3_out, not_4_out, not_5_out;

  not not_1 (not_1_out, A);
  not not_2 (not_2_out, B);
  not not_3 (not_3_out, D);
  not not_4 (not_4_out, A);
  not not_5 (not_5_out, C);
  and and_1 (DATA_0, not_1_out, not_2_out, C, not_3_out);
  and and_2 (DATA_1, not_4_out, not_5_out, D);
endmodule

module JAL_UC (
  input  A,
  input  B,
  input  C,
  input  D,
  output JAL
);

  wire not_1_out, not_2_out, not_3_out;

  not not_1 (not_1_out, A);
  not not_2 (not_2_out, B);
  not not_3 (not_3_out, C);
  and and_1 (JAL, not_1_out, not_2_out, not_3_out, D);
endmodule

module BGE_BLT_UC (
  input  A,
  input  B,
  input  C,
  input  D,
  output R
);

  wire not_1_out, not_2_out;

  not not_1 (not_1_out, A);
  not not_2 (not_2_out, D);
  and and_1 (R, not_1_out, B, C, not_2_out);
endmodule

module full_adder (
  input  Vi_menos_1,
  input  Ai,
  input  Bi,
  output Ri,
  output Vi
);

  wire and_1_out, and_2_out, or_2_out, xor_1_out;

  and and_1 (and_1_out, Bi, Ai);
  and and_2 (and_2_out, Vi_menos_1, or_2_out);
  or or_1 (Vi, and_1_out, and_2_out);
  or or_2 (or_2_out, Bi, Ai);
  xor xor_1 (xor_1_out, Ai, Bi);
  xor xor_2 (Ri, xor_1_out, Vi_menos_1);
endmodule

module add12b (
  input  [11:0] A,
  input  [11:0] B,
  output [11:0] R,
  output OVF
);

  wire full_adder_1_vi, full_adder_2_vi, full_adder_3_vi, full_adder_4_vi, full_adder_5_vi, full_adder_6_vi,
       full_adder_7_vi, full_adder_8_vi, full_adder_9_vi, full_adder_10_vi, full_adder_11_vi, not_1_out;

  not not_1 (not_1_out, 1'b1);
  full_adder full_adder_1 (.Vi_menos_1(not_1_out), .Ai(A[0]), .Bi(B[0]), .Ri(R[0]), .Vi(full_adder_1_vi));
  full_adder full_adder_2 (.Vi_menos_1(full_adder_1_vi), .Ai(A[1]), .Bi(B[1]), .Ri(R[1]), .Vi(full_adder_2_vi));
  full_adder full_adder_3 (.Vi_menos_1(full_adder_2_vi), .Ai(A[2]), .Bi(B[2]), .Ri(R[2]), .Vi(full_adder_3_vi));
  full_adder full_adder_4 (.Vi_menos_1(full_adder_3_vi), .Ai(A[3]), .Bi(B[3]), .Ri(R[3]), .Vi(full_adder_4_vi));
  full_adder full_adder_5 (.Vi_menos_1(full_adder_4_vi), .Ai(A[4]), .Bi(B[4]), .Ri(R[4]), .Vi(full_adder_5_vi));
  full_adder full_adder_6 (.Vi_menos_1(full_adder_5_vi), .Ai(A[5]), .Bi(B[5]), .Ri(R[5]), .Vi(full_adder_6_vi));
  full_adder full_adder_7 (.Vi_menos_1(full_adder_6_vi), .Ai(A[6]), .Bi(B[6]), .Ri(R[6]), .Vi(full_adder_7_vi));
  full_adder full_adder_8 (.Vi_menos_1(full_adder_7_vi), .Ai(A[7]), .Bi(B[7]), .Ri(R[7]), .Vi(full_adder_8_vi));
  full_adder full_adder_9 (.Vi_menos_1(full_adder_8_vi), .Ai(A[8]), .Bi(B[8]), .Ri(R[8]), .Vi(full_adder_9_vi));
  full_adder full_adder_10 (.Vi_menos_1(full_adder_9_vi), .Ai(A[9]), .Bi(B[9]), .Ri(R[9]), .Vi(full_adder_10_vi));
  full_adder full_adder_11 (.Vi_menos_1(full_adder_10_vi), .Ai(A[10]), .Bi(B[10]), .Ri(R[10]), .Vi(full_adder_11_vi));
  full_adder full_adder_12 (.Vi_menos_1(full_adder_11_vi), .Ai(A[11]), .Bi(B[11]), .Ri(R[11]), .Vi(OVF));
  // Probe on R
endmodule

module sub12b (
  input  [11:0] A,
  input  [11:0] B,
  output [11:0] R0,
  output OVF
);

  wire [11:0] not12b_1_r;

  not12b not12b_1 (.A(B), .R(not12b_1_r));
  add12b add12b_1 (.A(A), .B(not12b_1_r), .R(R0), .OVF(OVF));
endmodule

module not12b (
  input  [11:0] A,
  output [11:0] R
);

  wire [11:0] not_1_out;

  assign not_1_out = ~A;  // NOT_Gate not_1, 12 bits wide
  add12b add12b_1 (.A(not_1_out), .B(12'h1), .R(R));  // open: OVF

  // Notes on the sheet:
  //   soma 1
endmodule

module and12b (
  input  [11:0] A,
  input  [11:0] B,
  output [11:0] R
);

  assign R = A & B;  // AND_Gate and_1, 12 bits wide
endmodule

module mux12b (
  input  [11:0] A0_not,
  input  [11:0] A1_and,
  input  [11:0] A2_or,
  input  [11:0] A3_xor,
  input  [11:0] A4_add,
  input  [11:0] A5_sub,
  input  [11:0] A6_sll,
  input  [11:0] A7_srl,
  input  [3:0] S,
  output [11:0] R
);

  wire [11:0] bit_extender_1_out, bit_extender_2_out, bit_extender_3_out, bit_extender_4_out, not_1_out,
       not_2_out, not_3_out, not_4_out, not_5_out, not_6_out, not_7_out, not_8_out, not_9_out, not_10_out,
       not_11_out, not_12_out;

  assign bit_extender_1_out = {{11{S[0]}}, S[0]};  // Bit_Extender bit_extender_1
  assign bit_extender_2_out = {{11{S[1]}}, S[1]};  // Bit_Extender bit_extender_2
  assign bit_extender_3_out = {{11{S[2]}}, S[2]};  // Bit_Extender bit_extender_3
  assign bit_extender_4_out = {{11{S[3]}}, S[3]};  // Bit_Extender bit_extender_4
  assign not_1_out = ~bit_extender_1_out;  // NOT_Gate not_1, 12 bits wide
  assign not_2_out = ~bit_extender_2_out;  // NOT_Gate not_2, 12 bits wide
  assign not_3_out = ~bit_extender_3_out;  // NOT_Gate not_3, 12 bits wide
  assign not_4_out = ~bit_extender_2_out;  // NOT_Gate not_4, 12 bits wide
  assign not_5_out = ~bit_extender_3_out;  // NOT_Gate not_5, 12 bits wide
  assign not_6_out = ~bit_extender_1_out;  // NOT_Gate not_6, 12 bits wide
  assign not_7_out = ~bit_extender_3_out;  // NOT_Gate not_7, 12 bits wide
  assign not_8_out = ~bit_extender_3_out;  // NOT_Gate not_8, 12 bits wide
  assign not_9_out = ~bit_extender_1_out;  // NOT_Gate not_9, 12 bits wide
  assign not_10_out = ~bit_extender_2_out;  // NOT_Gate not_10, 12 bits wide
  assign not_11_out = ~bit_extender_2_out;  // NOT_Gate not_11, 12 bits wide
  assign not_12_out = ~bit_extender_1_out;  // NOT_Gate not_12, 12 bits wide
  assign R = A0_not & not_1_out & not_2_out & not_3_out & bit_extender_4_out;  // AND_Gate and_1, 12 bits wide
  assign R = A1_and & bit_extender_1_out & not_4_out & not_5_out & bit_extender_4_out;  // AND_Gate and_2, 12 bits wide
  assign R = A2_or & not_6_out & bit_extender_2_out & not_7_out & bit_extender_4_out;  // AND_Gate and_3, 12 bits wide
  assign R = A3_xor & bit_extender_1_out & bit_extender_2_out & not_8_out & bit_extender_4_out;  // AND_Gate and_4, 12 bits wide
  assign R = A4_add & not_9_out & not_10_out & bit_extender_3_out & bit_extender_4_out;  // AND_Gate and_5, 12 bits wide
  assign R = A5_sub & bit_extender_1_out & not_11_out & bit_extender_3_out & bit_extender_4_out;  // AND_Gate and_6, 12 bits wide
  assign R = A6_sll & not_12_out & bit_extender_2_out & bit_extender_3_out & bit_extender_4_out;  // AND_Gate and_7, 12 bits wide
  assign R = A7_srl & bit_extender_1_out & bit_extender_2_out & bit_extender_3_out & bit_extender_4_out;  // AND_Gate and_8, 12 bits wide

  // Notes on the sheet:
  //   S0 S1 S2 S3
endmodule

module xor12b (
  input  [11:0] A,
  input  [11:0] B,
  output [11:0] R
);

  assign R = A ^ B;  // XOR_Gate xor_1, 12 bits wide
endmodule

module or12b (
  input  [11:0] A,
  input  [11:0] B,
  output [11:0] R
);

  assign R = A | B;  // OR_Gate or_1, 12 bits wide
endmodule

module SLL12b (
  input  [11:0] A,
  input  [11:0] B,
  output [11:0] R
);

  Shifter #(.width(12)) shifter_1 (.in(A), .\dist (B[3:0]), .out(R));
endmodule

module SRL12b (
  input  [11:0] A,
  input  [11:0] B,
  output [11:0] R
);

  Shifter #(.shift("ar"), .width(12)) shifter_1 (.in(A), .\dist (B[3:0]), .out(R));
endmodule

module or_aux_ula (
  input  [11:0] A,
  output tell_if_ZERO
);

  wire or_1_out;

  or or_1 (or_1_out, A[0], A[1], A[2], A[3], A[4], A[5], A[6], A[7], A[8], A[9], A[10], A[11]);
  not not_1 (tell_if_ZERO, or_1_out);
endmodule

module mux_aux_ula (
  input  A0_add,
  input  A1_sub,
  input  A2_sll,
  input  [3:0] S,
  output OVF
);

  wire not_1_out, not_2_out, not_3_out, not_4_out;

  not not_1 (not_1_out, S[1]);
  not not_2 (not_2_out, S[0]);
  not not_3 (not_3_out, S[1]);
  not not_4 (not_4_out, S[0]);
  and and_1 (OVF, A0_add, not_1_out, not_2_out);
  and and_2 (OVF, A1_sub, not_3_out, S[0]);
  and and_3 (OVF, A2_sll, S[1], not_4_out);
endmodule

module unsig_ext_2b (
  input  [1:0] A,
  output [11:0] R
);

  assign R = {{9{1'b0}}, {1'b0, A}};  // Bit_Extender bit_extender_1
endmodule

module unsig_ext (
  input  [1:0] A,
  output [2:0] R
);


  assign R = {1'b0, A};
endmodule

module is_lt_0 (
  input  [11:0] A,
  output R
);


  assign R = A[11];
endmodule
